// Logisim project ex5.circ as structural Verilog: 6 circuits, main circuit rotr
module rotr (
  input  [15:0] A,
  input  [3:0] B,
  output [15:0] Out1
);

  proc proc_1 (.A(A), .B(B), .out_3(Out1));

  // Notes on the sheet:
  //   PUT CIRCUITRY HERE
endmodule

module rot8 (
  input  [15:0] in_1,
  output [15:0] out_2
);

  wire [15:0] rot4_1_out_2;

  rot4 rot4_1 (.in_1(in_1), .out_2(rot4_1_out_2));
  rot4 rot4_2 (.in_1(rot4_1_out_2), .out_2(out_2));

  // Notes on the sheet:
  //   PUT CIRCUITRY HERE
endmodule

module rot4 (
  input  [15:0] in_1,
  output [15:0] out_2
);

  wire [15:0] rot2_1_out_2;

  rot2 rot2_1 (.in_1(in_1), .out_2(rot2_1_out_2));
  rot2 rot2_2 (.in_1(rot2_1_out_2), .out_2(out_2));

  // Notes on the sheet:
  //   PUT CIRCUITRY HERE
endmodule

module rot2 (
  input  [15:0] in_1,
  output [15:0] out_2
);

  wire [15:0] rot1_1_out_2;

  rot1 rot1_1 (.in_1(in_1), .out_2(rot1_1_out_2));
  rot1 rot1_2 (.in_1(rot1_1_out_2), .out_2(out_2));

  // Notes on the sheet:
  //   PUT CIRCUITRY HERE
endmodule

module rot1 (
  input  [15:0] in_1,
  output [15:0] out_2
);


  assign out_2 = {in_1[0], in_1[15:1]};

  // Notes on the sheet:
  //   PUT CIRCUITRY HERE
endmodule

module proc (
  input  [15:0] A,
  input  [3:0] B,
  output [15:0] out_3
);

  wire [15:0] demultiplexer_1_out0, demultiplexer_1_out1, demultiplexer_2_out0, demultiplexer_2_out1,
       demultiplexer_3_out0, demultiplexer_3_out1, demultiplexer_4_out0, demultiplexer_4_out1,
       demultiplexer_5_out0, demultiplexer_5_out1, demultiplexer_6_out0, demultiplexer_6_out1,
       demultiplexer_7_out0, demultiplexer_7_out1, demultiplexer_8_out0, demultiplexer_8_out1,
       demultiplexer_9_out0, demultiplexer_9_out1, demultiplexer_10_out0, demultiplexer_10_out1,
       demultiplexer_11_out0, demultiplexer_11_out1, demultiplexer_12_out0, demultiplexer_12_out1,
       demultiplexer_13_out0, demultiplexer_13_out1, demultiplexer_14_out0, demultiplexer_14_out1,
       demultiplexer_15_out0, demultiplexer_15_out1, rot1_1_out_2, rot2_1_out_2, rot2_2_out_2, rot4_1_out_2,
       rot4_2_out_2, rot4_3_out_2, rot4_4_out_2, rot8_1_out_2, rot8_2_out_2, rot8_3_out_2, rot8_4_out_2,
       rot8_5_out_2, rot8_6_out_2, rot8_7_out_2, rot8_8_out_2;

  Demultiplexer #(.enable("false"), .width(16)) demultiplexer_1 (
    .out0(demultiplexer_1_out0), .out1(demultiplexer_1_out1), .in(A), .sel(B[0]));
  Demultiplexer #(.enable("false"), .width(16)) demultiplexer_2 (
    .out0(demultiplexer_2_out0), .out1(demultiplexer_2_out1), .in(demultiplexer_1_out0), .sel(B[1]));
  Demultiplexer #(.enable("false"), .width(16)) demultiplexer_3 (
    .out0(demultiplexer_3_out0), .out1(demultiplexer_3_out1), .in(demultiplexer_2_out0), .sel(B[2]));
  Demultiplexer #(.enable("false"), .width(16)) demultiplexer_4 (
    .out0(demultiplexer_4_out0), .out1(demultiplexer_4_out1), .in(demultiplexer_3_out0), .sel(B[3]));
  rot4 rot4_1 (.in_1(demultiplexer_3_out1), .out_2(rot4_1_out_2));
  rot8 rot8_1 (.in_1(demultiplexer_4_out1), .out_2(rot8_1_out_2));
  rot2 rot2_1 (.in_1(demultiplexer_2_out1), .out_2(rot2_1_out_2));
  Demultiplexer #(.enable("false"), .width(16)) demultiplexer_5 (
    .out0(demultiplexer_5_out0), .out1(demultiplexer_5_out1), .in(rot4_1_out_2), .sel(B[3]));
  rot8 rot8_2 (.in_1(demultiplexer_5_out1), .out_2(rot8_2_out_2));
  rot1 rot1_1 (.in_1(demultiplexer_1_out1), .out_2(rot1_1_out_2));
  Demultiplexer #(.enable("false"), .width(16)) demultiplexer_6 (
    .out0(demultiplexer_6_out0), .out1(demultiplexer_6_out1), .in(rot2_1_out_2), .sel(B[2]));
  Demultiplexer #(.enable("false"), .width(16)) demultiplexer_7 (
    .out0(demultiplexer_7_out0), .out1(demultiplexer_7_out1), .in(demultiplexer_6_out0), .sel(B[3]));
  rot8 rot8_3 (.in_1(demultiplexer_7_out1), .out_2(rot8_3_out_2));
  rot4 rot4_2 (.in_1(demultiplexer_6_out1), .out_2(rot4_2_out_2));
  Demultiplexer #(.enable("false"), .width(16)) demultiplexer_8 (
    .out0(demultiplexer_8_out0), .out1(demultiplexer_8_out1), .in(rot4_2_out_2), .sel(B[3]));
  assign out_3 = demultiplexer_4_out0 | rot8_1_out_2 | demultiplexer_5_out0 | rot8_2_out_2 | demultiplexer_7_out0 | rot8_3_out_2 | demultiplexer_8_out0 | rot8_4_out_2 | demultiplexer_10_out0 | rot8_5_out_2 | demultiplexer_12_out0 | rot8_6_out_2 | demultiplexer_14_out0 | rot8_7_out_2 | demultiplexer_15_out0 | rot8_8_out_2;  // OR_Gate or_1, 16 bits wide
  rot8 rot8_4 (.in_1(demultiplexer_8_out1), .out_2(rot8_4_out_2));
  Demultiplexer #(.enable("false"), .width(16)) demultiplexer_9 (
    .out0(demultiplexer_9_out0), .out1(demultiplexer_9_out1), .in(demultiplexer_11_out0), .sel(B[2]));
  Demultiplexer #(.enable("false"), .width(16)) demultiplexer_10 (
    .out0(demultiplexer_10_out0), .out1(demultiplexer_10_out1), .in(demultiplexer_9_out0), .sel(B[3]));
  Demultiplexer #(.enable("false"), .width(16)) demultiplexer_11 (
    .out0(demultiplexer_11_out0), .out1(demultiplexer_11_out1), .in(rot1_1_out_2), .sel(B[1]));
  rot8 rot8_5 (.in_1(demultiplexer_10_out1), .out_2(rot8_5_out_2));
  rot2 rot2_2 (.in_1(demultiplexer_11_out1), .out_2(rot2_2_out_2));
  rot4 rot4_3 (.in_1(demultiplexer_9_out1), .out_2(rot4_3_out_2));
  Demultiplexer #(.enable("false"), .width(16)) demultiplexer_12 (
    .out0(demultiplexer_12_out0), .out1(demultiplexer_12_out1), .in(rot4_3_out_2), .sel(B[3]));
  rot8 rot8_6 (.in_1(demultiplexer_12_out1), .out_2(rot8_6_out_2));
  Demultiplexer #(.enable("false"), .width(16)) demultiplexer_13 (
    .out0(demultiplexer_13_out0), .out1(demultiplexer_13_out1), .in(rot2_2_out_2), .sel(B[2]));
  Demultiplexer #(.enable("false"), .width(16)) demultiplexer_14 (
    .out0(demultiplexer_14_out0), .out1(demultiplexer_14_out1), .in(demultiplexer_13_out0), .sel(B[3]));
  rot4 rot4_4 (.in_1(demultiplexer_13_out1), .out_2(rot4_4_out_2));
  rot8 rot8_7 (.in_1(demultiplexer_14_out1), .out_2(rot8_7_out_2));
  Demultiplexer #(.enable("false"), .width(16)) demultiplexer_15 (
    .out0(demultiplexer_15_out0), .out1(demultiplexer_15_out1), .in(rot4_4_out_2), .sel(B[3]));
  rot8 rot8_8 (.in_1(demultiplexer_15_out1), .out_2(rot8_8_out_2));
endmodule
